# Fritzing sketch CIRC16 (saved by Fritzing 0.9.3b)
breadboards: 1

parts:
  Part2 = Adafruit Metro with Headers [part_number="Adafruit #2488"]
  IR1 = TSOP312.., 314.. [package=THT]
  R1 = Resistor [tolerance=±5% resistance=560 package=THT]
  LED1 = Infrared LED - 5mm [package="5 mm [THT]"]  # not connected

nets:
  N1: Part2.IO8, R1.Pin_1
  N2: Part2.IO5, IR1.GND
  N3: Part2.3.3V, IR1.Data
  N4: Part2.GND, IR1.Vs

custom parts:
  Adafruit Metro with Headers: We sure love the ATmega328 here at Adafruit, and we use them a lot for our own projects. The processor has plenty of GPIO, Analog inputs, hardware UART SPI and I2C, timers and PWM galore - just enough for most simple projects. When we need to go small, we use a Pro Trinket 3V or 5V, but when size isn't as much of a concern, and an USB-serial converter is required, we reach for an Adafruit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
  Infrared LED - 5mm: A generic infrared LED (~1.2V)
