# Fritzing sketch circ01 (saved by Fritzing 0.9.3b)
breadboards: 1

parts:
  Part1 = Adafruit Metro with Headers [part_number="Adafruit #2488"]
  LED2 = LEDs [package=led10mm]
  R1 = Resistor [tolerance=±5% resistance=560 package=THT]

nets:
  N1: Part1.SCK, LED2.A
  N2: Part1.GND, R1.Pin_1
  N3: LED2.C, R1.Pin_0

custom parts:
  Adafruit Metro with Headers: We sure love the ATmega328 here at Adafruit, and we use them a lot for our own projects. The processor has plenty of GPIO, Analog inputs, hardware UART SPI and I2C, timers and PWM galore - just enough for most simple projects. When we need to go small, we use a Pro Trinket 3V or 5V, but when size isn't as much of a concern, and an USB-serial converter is required, we reach for an Adafruit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
