# Fritzing sketch circ07 (saved by Fritzing 0.9.3b)
breadboards: 1

parts:
  Part2 = Adafruit Metro with Headers [part_number="Adafruit #2488"]
  S1 = Pushbutton [package="[THT]"]
  S2 = Pushbutton [package="[THT]"]
  R1 = Resistor [tolerance=±5% resistance=10k package=THT]
  R2 = Resistor [tolerance=±5% resistance=10k package=THT]
  R3 = Resistor [tolerance=±5% resistance=560 package=THT]
  LED1 = LED - 5mm [color="Red (633nm)" package="5 mm [THT]"]

nets:
  N1: Part2.SCK, LED1.anode
  N2: Part2.IO3, S2.Pin_3, S2.Pin_4, R2.Pin_0
  N3: Part2.IO2, S1.Pin_3, S1.Pin_4, R1.Pin_0
  N4: Part2.3.3V, R1.Pin_1, R2.Pin_1
  N5: Part2.GND, S1.Pin_1, S1.Pin_2, S2.Pin_1, S2.Pin_2, R3.Pin_1
  N6: R3.Pin_0, LED1.cathode

notes:
  on

custom parts:
  Adafruit Metro with Headers: We sure love the ATmega328 here at Adafruit, and we use them a lot for our own projects. The processor has plenty of GPIO, Analog inputs, hardware UART SPI and I2C, timers and PWM galore - just enough for most simple projects. When we need to go small, we use a Pro Trinket 3V or 5V, but when size isn't as much of a concern, and an USB-serial converter is required, we reach for an Adafruit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
