# Fritzing sketch circ08 (saved by Fritzing 0.9.3b)
breadboards: 1

parts:
  R1 = Resistor [tolerance=±5% resistance=560 package=THT]
  POT1 = Breadboard Trimpot
  Part2 = Adafruit Metro with Headers [part_number="Adafruit #2488"]
  LED1 = LED - 5mm [color="Red (635nm)" package="5 mm [THT]"]

nets:
  N1: R1.Pin_0, POT1.PIN1, Part2.GND
  N2: R1.Pin_1, LED1.cathode
  N3: POT1.PIN2, Part2.AD0
  N4: POT1.PIN3, Part2.+5V
  N5: Part2.SCK, LED1.anode

custom parts:
  Adafruit Metro with Headers: We sure love the ATmega328 here at Adafruit, and we use them a lot for our own projects. The processor has plenty of GPIO, Analog inputs, hardware UART SPI and I2C, timers and PWM galore - just enough for most simple projects. When we need to go small, we use a Pro Trinket 3V or 5V, but when size isn't as much of a concern, and an USB-serial converter is required, we reach for an Adafruit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
