# Fritzing sketch circ12 (saved by Fritzing 0.9.3b)
breadboards: 1

parts:
  Part2 = Adafruit Metro with Headers [part_number="Adafruit #2488"]
  LED1 = RGB LED (com. cathode, rbg) [package="5 mm [THT]"]
  R1 = Resistor [tolerance=±5% resistance=560 package=THT]
  R2 = Resistor [tolerance=±5% resistance=560 package=THT]
  R3 = Resistor [tolerance=±5% resistance=560 package=THT]

nets:
  N1: Part2.MOSI, R2.Pin_1
  N2: Part2.SS, R3.Pin_1
  N3: Part2.IO9, R1.Pin_1
  N4: Part2.3.3V, LED1.common_cathode
  N5: LED1.red_anode, R1.Pin_0
  N6: LED1.blue_anode, R2.Pin_0
  N7: LED1.green_anode, R3.Pin_0

custom parts:
  Adafruit Metro with Headers: We sure love the ATmega328 here at Adafruit, and we use them a lot for our own projects. The processor has plenty of GPIO, Analog inputs, hardware UART SPI and I2C, timers and PWM galore - just enough for most simple projects. When we need to go small, we use a Pro Trinket 3V or 5V, but when size isn't as much of a concern, and an USB-serial converter is required, we reach for an Adafruit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
