# Fritzing sketch CIRC03-express (saved by Fritzing 0.9.3b)
breadboards: 1

parts:
  M1 = DC Motor
  Q1 = NPN-Transistor [package="SOT-23 [SMD]"]
  D2 = P1000K [part_number=P1000K]
  R1 = Resistor [tolerance=±5% resistance=2.2k package="2512 [SMD]"]
  Part3 = Adafruit Metro M0 Express

nets:
  N1: M1.pin_1, D2.cathode, Part3.3.3V
  N2: M1.pin_2, Q1.1, D2.anode
  N3: Q1.2, Part3.GND
  N4: Q1.0, R1.Pin_1
  N5: R1.Pin_0, Part3.D9

notes:
  Emitter
  Base
  Collector
  -
  +

custom parts:
  Adafruit Metro M0 Express: Metro is our series of microcontroller boards for use with the Arduino IDE. This new Metro board looks a whole lot like our original Metro 328, but with a huge upgrade. Instead of the ATmega328, this Metro features a ATSAMD21G18 chip, an ARM Cortex M0+. It's our first Metro that is designed for use with CircuitPython! CircuitPython is our beginner-oriented flavor of MicroPython - and as the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
