# Fritzing sketch CIRC05-express (saved by Fritzing 0.9.3b)
breadboards: 1

parts:
  Part3 = Adafruit Metro M0 Express
  R8 = Resistor [tolerance=±5% resistance=560 package=THT]
  R7 = Resistor [tolerance=±5% resistance=560 package=THT]
  R5 = Resistor [tolerance=±5% resistance=560 package=THT]
  R6 = Resistor [tolerance=±5% resistance=560 package=THT]
  LED2 = LED Red 3mm - Top View [package="3 mm [THT] Top View"]
  LED1 = LED Red 3mm - Top View [package="3 mm [THT] Top View"]
  LED4 = LED Red 3mm - Top View [package="3 mm [THT] Top View"]
  LED3 = LED Red 3mm - Top View [package="3 mm [THT] Top View"]
  LED7 = LED Red 3mm - Top View [package="3 mm [THT] Top View"]
  LED8 = LED Red 3mm - Top View [package="3 mm [THT] Top View"]
  R4 = Resistor [tolerance=±5% resistance=560 package=THT]
  R3 = Resistor [tolerance=±5% resistance=560 package=THT]
  R2 = Resistor [tolerance=±5% resistance=560 package=THT]
  R1 = Resistor [tolerance=±5% resistance=560 package=THT]
  LED6 = LED Red 3mm - Top View [package="3 mm [THT] Top View"]
  LED5 = LED Red 3mm - Top View [package="3 mm [THT] Top View"]
  U1 = 74HC595 [package="DIP16 [THT]"]

nets:
  N1: Part3.D4, U1.ST_CP
  N2: Part3.D3, U1.SH_CP
  N3: Part3.D2, U1.DS
  3.3V: Part3.3.3V, U1.MR, U1.VCC
  GND: Part3.GND, R8.Pin_1, R7.Pin_1, R5.Pin_1, R6.Pin_1, R4.Pin_1, R3.Pin_1, R2.Pin_1, R1.Pin_1, U1.GND, U1.OE
  N4: R8.Pin_0, LED4.cathode
  N5: R7.Pin_0, LED3.cathode
  N6: R5.Pin_0, LED1.cathode
  N7: R6.Pin_0, LED2.cathode
  N8: LED7.cathode, R3.Pin_0
  N9: LED8.cathode, R4.Pin_0
  N10: R2.Pin_0, LED6.cathode
  N11: R1.Pin_0, LED5.cathode

custom parts:
  Adafruit Metro M0 Express: Metro is our series of microcontroller boards for use with the Arduino IDE. This new Metro board looks a whole lot like our original Metro 328, but with a huge upgrade. Instead of the ATmega328, this Metro features a ATSAMD21G18 chip, an ARM Cortex M0+. It's our first Metro that is designed for use with CircuitPython! CircuitPython is our beginner-oriented flavor of MicroPython - and as the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
  LED Red 3mm - Top View: A generic red LED (~1.8V)
