# Fritzing sketch CIRC07-express (saved by Fritzing 0.9.3b)
breadboards: 1

parts:
  LED1 = LED - 5mm [color="Red (633nm)" package="5 mm [THT]"]
  S1 = Pushbutton [package="[THT]"]
  S2 = Pushbutton [package="[THT]"]
  R1 = Resistor [tolerance=±5% resistance=10k package=THT]
  R2 = Resistor [tolerance=±5% resistance=10k package=THT]
  R3 = Resistor [tolerance=±5% resistance=560 package=THT]
  Part3 = Adafruit Metro M0 Express

nets:
  N1: LED1.cathode, R3.Pin_0
  N2: LED1.anode, Part3.D13
  N3: S1.Pin_1, S1.Pin_2, S2.Pin_1, S2.Pin_2, R3.Pin_1, Part3.GND
  N4: S1.Pin_3, S1.Pin_4, R1.Pin_0, Part3.D2
  N5: S2.Pin_3, S2.Pin_4, R2.Pin_0, Part3.D3
  N6: R1.Pin_1, R2.Pin_1, Part3.3.3V

notes:
  on

custom parts:
  Adafruit Metro M0 Express: Metro is our series of microcontroller boards for use with the Arduino IDE. This new Metro board looks a whole lot like our original Metro 328, but with a huge upgrade. Instead of the ATmega328, this Metro features a ATSAMD21G18 chip, an ARM Cortex M0+. It's our first Metro that is designed for use with CircuitPython! CircuitPython is our beginner-oriented flavor of MicroPython - and as the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
