# Fritzing sketch CIRC15-express (saved by Fritzing 0.9.3b)
breadboards: 1

parts:
  Part3 = Adafruit Metro M0 Express
  IR1 = TSOP312.., 314.. [package=THT]
  LED1 = LED - 5mm [color="Red (633nm)" package="5 mm [THT]"]
  R1 = Resistor [tolerance=±5% resistance=560 package=THT]

nets:
  N1: Part3.D11, LED1.anode
  N2: Part3.D6, IR1.GND
  N3: Part3.GND, IR1.Vs, R1.Pin_0
  N4: LED1.cathode, R1.Pin_1

custom parts:
  Adafruit Metro M0 Express: Metro is our series of microcontroller boards for use with the Arduino IDE. This new Metro board looks a whole lot like our original Metro 328, but with a huge upgrade. Instead of the ATmega328, this Metro features a ATSAMD21G18 chip, an ARM Cortex M0+. It's our first Metro that is designed for use with CircuitPython! CircuitPython is our beginner-oriented flavor of MicroPython - and as the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
