# Fritzing sketch CIRC16-express (saved by Fritzing 0.9.3b)
breadboards: 1

parts:
  IR1 = TSOP312.., 314.. [package=THT]
  LED2 = LED - 5mm [color="Red (633nm)" package="5 mm [THT]"]
  R2 = Resistor [tolerance=±5% resistance=560 package=THT]
  Part3 = Adafruit Metro M0 Express

nets:
  N1: IR1.GND, Part3.D6
  N2: IR1.Vs, R2.Pin_0, Part3.GND
  N3: IR1.Data, Part3.3.3V
  N4: LED2.cathode, R2.Pin_1
  N5: LED2.anode, Part3.D13

custom parts:
  Adafruit Metro M0 Express: Metro is our series of microcontroller boards for use with the Arduino IDE. This new Metro board looks a whole lot like our original Metro 328, but with a huge upgrade. Instead of the ATmega328, this Metro features a ATSAMD21G18 chip, an ARM Cortex M0+. It's our first Metro that is designed for use with CircuitPython! CircuitPython is our beginner-oriented flavor of MicroPython - and as the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
