# Fritzing sketch CIRC18-express (saved by Fritzing 0.9.3b)
breadboards: 1

parts:
  Part3 = Adafruit Metro M0 Express
  S1 = Pushbutton [package="[THT]"]
  POT1 = Breadboard Trimpot
  R1 = Resistor [tolerance=±5% resistance=10k package=THT]

nets:
  N1: Part3.A0, POT1.PIN2
  N2: Part3.D6, S1.Pin_3, S1.Pin_4, R1.Pin_1
  N3: Part3.3.3V, POT1.PIN1, R1.Pin_0
  N4: Part3.GND, S1.Pin_1, S1.Pin_2, POT1.PIN3

custom parts:
  Adafruit Metro M0 Express: Metro is our series of microcontroller boards for use with the Arduino IDE. This new Metro board looks a whole lot like our original Metro 328, but with a huge upgrade. Instead of the ATmega328, this Metro features a ATSAMD21G18 chip, an ARM Cortex M0+. It's our first Metro that is designed for use with CircuitPython! CircuitPython is our beginner-oriented flavor of MicroPython - and as the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
